# Fritzing sketch espParking (saved by Fritzing 1.0.2b)
breadboards: 2

parts:
  U1 = ESP8266 NodeMCU LoLin module
  YwRobot_Power_Supply1 = YwRobot Breadboard Power Supply [part_number=545043]  # not connected
  LED1 = LED - 5mm [color="Green (570nm)" current=0.030A package="5 mm [THT]"]
  LED2 = LED - 5mm [color="Red (633nm)" current=0.030A package="5 mm [THT]"]
  R1 = Resistor [tolerance=±5% resistance=220 package="0805 [SMD]"]
  R2 = Resistor [tolerance=±5% resistance=220 package="0805 [SMD]"]
  M1 = Dagu DGServo 9g (Top view) [part_number=RS001B]

nets:
  N1: U1.D1, LED1.anode
  N2: U1.D2, LED2.anode
  N3: U1.D4, M1.pulse
  GND: U1.GND, R1.Pin_0, R2.Pin_0, M1.gnd
  VIN: U1.Vin, M1.vcc
  N4: LED1.cathode, R1.Pin_1
  N5: LED2.cathode, R2.Pin_1

custom parts:
  ESP8266 NodeMCU LoLin module: ESP8266 based NodeMCU
  YwRobot Breadboard Power Supply: The YwRobot Breadboard Power Supply (MB-V2) has two power rails; they can be 5V or 3V3. Power to the module can be provided through the female USB socket or through the A10 (female) 2.1mm power jack.
