# Fritzing sketch picoRoom (saved by Fritzing 1.0.2b)
breadboards: 2

parts:
  Mod1 = Raspberry Pi Pico W
  Part1 = RFID-RC522-v2
  Part2 = RFID-RC522-v2
  Keypad4x1 = Keypad Membran 4x4
  LCM1602_IIC1 = LCM1602 IIC [part_number="LCM1602 IIC" chip_label="LCM1602 IIC" package="DIP (Dual Inline) [THT]"]
  U2 = LCD-16X2 [package=lcd-16x2_noholes]
  LED1 = LED - 3mm [color="Green (570nm)" current=0.030A package="3 mm [THT]"]
  LED2 = LED - 3mm [color="Red (660nm)" current=0.030A package="3 mm [THT]"]
  R2 = Resistor [tolerance=±5% power=0.25W resistance=220 package=THT]
  R3 = Resistor [tolerance=±5% power=0.25W resistance=220 package=THT]
  S1 = Pushbutton [package="[THT]"]
  R4 = Resistor [tolerance=±5% power=0.25W resistance=220 package=THT]
  YwRobot_Power_Supply1 = YwRobot Breadboard Power Supply [part_number=545043]  # not connected

nets:
  N1: Mod1.pin_1, S1.Pin_1, S1.Pin_2
  N2: Mod1.pin_2, Part2.SDA
  GND: Mod1.pin_3, Mod1.pin_8, Mod1.pin_13, Mod1.pin_18, Mod1.pin_23, Mod1.pin_28, Mod1.pin_33, Mod1.pin_38, Mod1.pin_42, Part1.GND, Part2.GND, R2.Pin_0, R3.Pin_0, R4.Pin_1
  N3: Mod1.pin_4, Part2.SCK
  N4: Mod1.pin_5, Part2.MOSI
  N5: Mod1.pin_6, Part2.MISO
  N6: Mod1.pin_7, Part2.RST
  N7: Mod1.pin_9, LED1.anode
  N8: Mod1.pin_10, LED2.anode
  N9: Mod1.pin_12, Part1.SDA
  N10: Mod1.pin_14, Part1.SCK
  N11: Mod1.pin_15, Part1.MOSI
  N12: Mod1.pin_16, Part1.MISO
  N13: Mod1.pin_17, Part1.RST
  N14: Mod1.pin_19, LCM1602_IIC1.SDA
  N15: Mod1.pin_20, LCM1602_IIC1.SCL
  N16: Mod1.pin_21, Keypad4x1.Pin1
  N17: Mod1.pin_22, Keypad4x1.Pin2
  N18: Mod1.pin_24, Keypad4x1.Pin3
  N19: Mod1.pin_25, Keypad4x1.Pin4
  N20: Mod1.pin_26, Keypad4x1.Pin5
  N21: Mod1.pin_27, Keypad4x1.Pin6
  N22: Mod1.pin_29, Keypad4x1.Pin7
  N23: Mod1.pin_31, Keypad4x1.Pin8
  3.3V: Mod1.pin_36, Part1.3.3V, Part2.3.3V
  N24: Mod1.pin_39, S1.Pin_3, S1.Pin_4
  VSS: LCM1602_IIC1.VSS, U2.VSS
  VDD: LCM1602_IIC1.VDD, U2.VDD
  N25: LCM1602_IIC1.V0, U2.VO
  N26: LCM1602_IIC1.RS, U2.RS
  N27: LCM1602_IIC1.RW, U2.R_W
  N28: LCM1602_IIC1.E, U2.E
  N29: LCM1602_IIC1.D0, U2.DB0
  N30: LCM1602_IIC1.D1, U2.DB1
  N31: LCM1602_IIC1.D2, U2.DB2
  N32: LCM1602_IIC1.D3, U2.DB3
  N33: LCM1602_IIC1.D4, U2.DB4
  N34: LCM1602_IIC1.D5, U2.DB5
  N35: LCM1602_IIC1.D6, U2.DB6
  N36: LCM1602_IIC1.D7, U2.DB7
  N37: LCM1602_IIC1.A, U2.A
  N38: LCM1602_IIC1.K, U2.K
  N39: LED1.cathode, R3.Pin_1
  N40: LED2.cathode, R2.Pin_1

custom parts:
  Raspberry Pi Pico W: Raspberry Pi Pico W. Based around the RP2040 microcontroller the Pico W is a low cost microcontroller device bringing Raspberry Pi quality, cost, and easy of use to the microcontroller space. The areas marked KEEPOUT in pcb silkscreen should not have traces running through them to avoid shorts on a soldered in module!
  RFID-RC522-v2: A simple China made RFID-RC522 Reader; do check the pin labels, as this is a MFRC522 based clone.
  Keypad Membran 4x4: Membrane Keypad 4x4 Matrix
  LCM1602 IIC: I2C-Module to use a 1602 or 2004 LCD on with the wire.h libory Serial LCD Modul
  YwRobot Breadboard Power Supply: The YwRobot Breadboard Power Supply (MB-V2) has two power rails; they can be 5V or 3V3. Power to the module can be provided through the female USB socket or through the A10 (female) 2.1mm power jack.
