# Fritzing sketch MQ5_buzzer (saved by Fritzing 1.0.2b)
breadboards: 1

parts:
  YwRobot_Power_Supply1 = YwRobot Breadboard Power Supply [part_number=545043]
  Mod1 = MQ-7 breakout
  J1 = Piezo Speaker
  R1 = Resistor [tolerance=±5% resistance=2.2k package="0805 [SMD]"]
  R2 = Resistor [tolerance=±5% resistance=1k package="0805 [SMD]"]
  Q1 = TRANSISTOR_NPN [package=to-92-ammo]
  Q2 = TRANSISTOR_NPN [package=to-92-ammo]
  C1 = Ceramic Capacitor [capacitance=0.47mF voltage=35V package="0805 [SMD, multilayer]"]

nets:
  N1: YwRobot_Power_Supply1.VCC#5, Mod1.VCC, R2.Pin_1, Q2.C
  N2: YwRobot_Power_Supply1.GND#11, Mod1.GND, Q1.E, C1.0
  N3: YwRobot_Power_Supply1.GND#13, J1.pin1
  N4: Mod1.DO, R1.Pin_0, C1.1
  N5: J1.pin2, Q2.E
  N6: R1.Pin_1, Q1.B
  N7: R2.Pin_0, Q1.C, Q2.B

custom parts:
  YwRobot Breadboard Power Supply: The YwRobot Breadboard Power Supply (MB-V2) has two power rails; they can be 5V or 3V3. Power to the module can be provided through the female USB socket or through the A10 (female) 2.1mm power jack.
  MQ-7 breakout: MQ-5 gas sensor
